# Fritzing sketch wiring_schematic (saved by Fritzing 0.7.1b)
breadboards: 1
perfboards: 1

parts:
  U1 = XBee
  Teensy1 = Teensy 2.0
  M1 = DC Motor  # not connected
  M2 = DC Motor  # not connected
  VCC1 = Battery block 9V  # not connected
  VCC2 = Battery

nets:
  VCC: U1.VCC, Teensy1.VCC, VCC2.+
  N1: U1.pin2, Teensy1.D3
  N2: U1.pin3, Teensy1.D2
  GND: U1.pin5, U1.GND, Teensy1.GND, VCC2.-

notes:
  Note: this is actually this
  part: http://www.pololu.com/catalog/product/713
  but since Fritzing doesn't include this part, we can't
  really use it, hence the simple perfboard
